# Fritzing sketch MEGA_circuit_diagram (saved by Fritzing 0.9.3b)

parts:
  U1 = LCD-16X2 [package=lcd-16x2_nosilk]
  LCM1602_IIC1 = LCM1602 IIC [part_number="LCM1602 IIC" chip_label="LCM1602 IIC" package="DIP (Dual Inline) [THT]"]
  Part2 = Arduino Mega ADK (Rev3)

nets:
  VSS: U1.VSS, LCM1602_IIC1.VSS
  VDD: U1.VDD, LCM1602_IIC1.VDD
  N1: U1.VO, LCM1602_IIC1.V0
  N2: U1.RS, LCM1602_IIC1.RS
  N3: U1.R_W, LCM1602_IIC1.RW
  N4: U1.E, LCM1602_IIC1.E
  N5: U1.DB0, LCM1602_IIC1.D0
  N6: U1.DB1, LCM1602_IIC1.D1
  N7: U1.DB2, LCM1602_IIC1.D2
  N8: U1.DB3, LCM1602_IIC1.D3
  N9: U1.DB4, LCM1602_IIC1.D4
  N10: U1.DB5, LCM1602_IIC1.D5
  N11: U1.DB6, LCM1602_IIC1.D6
  N12: U1.DB7, LCM1602_IIC1.D7
  N13: U1.A, LCM1602_IIC1.A
  N14: U1.K, LCM1602_IIC1.K
  GND: LCM1602_IIC1.GND, Part2.GND
  VCC: LCM1602_IIC1.VCC, Part2.5V
  N15: LCM1602_IIC1.SDA, Part2.D20/SDA
  N16: LCM1602_IIC1.SCL, Part2.D21/SCL
  N17: LCM1602_IIC1.LED_A, LCM1602_IIC1.LED_B

custom parts:
  LCM1602 IIC: I2C-Module to use a 1602 or 2004 LCD on with the wire.h libory Serial LCD Modul
